# Fritzing sketch batbox (saved by Fritzing 0.9.3b)

parts:
  Part2 = Arduino Nano (Rev3.0)
  Part4 = Real Time Clock Module - DS1307 RTC Breakout Board
  SD_card_module1 = SD Card Module

nets:
  GND: Part2.GND, Part4.GND, SD_card_module1.GND
  N1: Part2.D4, SD_card_module1.CS
  N2: Part2.D11/MOSI, SD_card_module1.MOSI
  N3: Part2.D12/MISO, SD_card_module1.MISO
  5V: Part2.5V, Part4.5V
  N4: Part2.A5, Part4.SCL
  N5: Part2.A4, Part4.SDA
  N6: Part2.3V3, SD_card_module1.+3.3
  N7: Part2.D13/SCK, SD_card_module1.SCK

custom parts:
  SD Card Module: SD Card Module Slot Socket Reader For Arduino ARM MCU
